# Fritzing sketch frizting_hello_world (saved by Fritzing 0.9.6b)
breadboards: 2

parts:
  Part1 = Adafruit HUZZAH32 ESP32 Feather [part_number="Adafruit #3405"]
  LED1 = LEDs [package=led10mm]
  R1 = Resistor [tolerance=±5% resistance=100 package="1206 [SMD]"]

nets:
  N1: Part1.GND, R1.Pin_0
  N2: Part1.IO13_A12, LED1.A
  N3: LED1.C, R1.Pin_1
