# Fritzing sketch frizting_hello_world (saved by Fritzing 0.9.6b)
breadboards: 2

parts:
  Part1 = Adafruit HUZZAH32 ESP32 Feather [part_number="Adafruit #3405"]
  LED1 = LEDs [package=led10mm]
  R1 = Resistor [tolerance=±5% resistance=100 package="1206 [SMD]"]
  Part2 = Adafruit HUZZAH32 ESP32 Feather [part_number="Adafruit #3405"]
  LED2 = LEDs [package=led10mm]
  LED3 = LEDs [package=led10mm]
  LED4 = LEDs [package=led10mm]
  R2 = Resistor [tolerance=±5% resistance=100 package="1206 [SMD]"]
  R3 = Resistor [tolerance=±5% resistance=100 package="1206 [SMD]"]
  R4 = Resistor [tolerance=±5% resistance=100 package="1206 [SMD]"]

nets:
  N1: Part1.GND, R1.Pin_0
  N2: Part1.IO13_A12, LED1.A
  N3: LED1.C, R1.Pin_1
  N4: Part2.GND, R2.Pin_0, R3.Pin_0, R4.Pin_0
  N5: Part2.IO13_A12, LED2.A
  N6: Part2.IO12_A11, LED3.A
  N7: Part2.IO27_A10, LED4.A
  N8: LED2.C, R2.Pin_1
  N9: LED3.C, R3.Pin_1
  N10: LED4.C, R4.Pin_1
